# Fritzing sketch Electronique_Projet_DI (saved by Fritzing 0.9.3b)
circuit board: 10.1775cm x 5.33049cm
breadboards: 1

parts:
  Arduino_MEGA_2560_R3 = Arduino Mega 2560 (Rev3)
  ESP8266 = ESP8266 WiFi Module [part_number=ESP8266]
  DHT22 = DHT22 Humidity and Temperature Sensor
  R1 = Resistor [tolerance=±5% resistance=220 package=THT]
  Photoresistance = PHOTOCELL [package=photocell]

nets:
  N1: Arduino_MEGA_2560_R3.A0, R1.Pin_0, Photoresistance.P$2
  N2: Arduino_MEGA_2560_R3.D19/RX1, ESP8266.TXD
  N3: Arduino_MEGA_2560_R3.D18/TX1, ESP8266.RXD
  GND: Arduino_MEGA_2560_R3.GND, ESP8266.GND, DHT22.GND, R1.Pin_1
  3V3: Arduino_MEGA_2560_R3.3V3, ESP8266.VCC, ESP8266.CH_PD
  5V: Arduino_MEGA_2560_R3.5V, DHT22.VDD, Photoresistance.P$1
  N4: Arduino_MEGA_2560_R3.D3_PWM, DHT22.DATA

custom parts:
  ESP8266 WiFi Module: Generic WiFi Module based on the ESP8266 with onboard PCB antenna and UART communications

// code stored in the sketch: MonServeur.ino
/*
 For more details see: http://yaab-arduino.blogspot.com/p/wifiesp.html
*/

//Lucas CHACON & Alexandre BUREAU

#include "WiFiEsp.h"

#include "DHT.h"
#define DHTPIN 3
#define DHTTYPE DHT22

// Emulate Serial1 on pins 18/19 if not present
#ifndef HAVE_HWSERIAL1
#include "SoftwareSerial.h"
SoftwareSerial Serial1(18, 19); // RX, TX
#endif

char ssid[] = "Lucas's wifi_2.4GHz";// your network SSID (name)
char pass[] = "Lucas-93";        // your network password

//char ssid[] = "Asus";
//char pass[] = "12345678";

int status = WL_IDLE_STATUS;     // the Wifi radio's status
int reqCount = 0;                // number of requests received

WiFiEspServer server(80);

const char Pin_lum = A0;

DHT dht(DHTPIN, DHTTYPE);

void setup()
{
 
  // initialize serial for debugging
  Serial.begin(115200);
  // initialize serial for ESP module
  Serial1.begin(115200);
  // initialize ESP module
  WiFi.init(&Serial1);

  // check for the presence of the shield
  if (WiFi.status() == WL_NO_SHIELD) {
    Serial.println("WiFi shield not present");
    // don't continue
    while (true);
  }

  // attempt to connect to WiFi network
  while ( status != WL_CONNECTED) {
    Serial.print("Attempting to connect to WPA SSID: ");
    Serial.println(ssid);
    // Connect to WPA/WPA2 network
    status = WiFi.begin(ssid, pass);
  }

  Serial.println("You're connected to the network");
  printWifiStatus();
  Serial.println("debut connexion" ) ; 
  // start the web server on port 80
  server.begin();

   //Init capteur temperature
   dht.begin(); 
}


void loop()
{
  int lumiere = analogRead(Pin_lum); 
  float humidity = dht.readHumidity();
  float temperature = dht.readTemperature();
  float idx_temp = dht.computeHeatIndex(temperature, humidity, false);

//  if (isnan(humidity) || isnan(temperature)) {
//    Serial.println(F("Echec de connexion au capteur !"));
//    return;
//  }
  
  // listen for incoming clients
  WiFiEspClient client = server.available();
  if (client) {
    Serial.println("New client");
    // an http request ends with a blank line
    boolean currentLineIsBlank = true;
    while (client.connected()) {
      if (client.available()) {
        char c = client.read();
        Serial.write(c);
        // if you've gotten to the end of the line (received a newline
        // character) and the line is blank, the http request has ended,
        // so you can send a reply
        if (c == '\n' && currentLineIsBlank) {
          Serial.println("Sending response");
          
          // send a standard http response header
          // use \r\n instead of many println statements to speedup data send
          client.print(
            "HTTP/1.1 200 OK\r\n"
            "Content-Type: text/html\r\n"
            "Connection: close\r\n"  // the connection will be closed after completion of the response
            "Refresh: 5\r\n"        // refresh the page automatically every 20 sec
            "\r\n");
          //client.print("<link href = 'Mapage.css' rel = 'stylesheet'>")
          client.print("<!DOCTYPE HTML>\r\n");
          client.print("<html>\r\n");
          client.print("<h1>Sonde Meteo</h1>\r\n"); //<hn> + n grand + police petite (toujours en gras)
          client.print("<p>Valeurs :\r\n");
          client.print("<br>\r\n");
          client.print("Luminosity: ");
          client.print(lumiere);
          client.print(" lum");
          client.print("<br>\r\n");
          client.print("Humidity: ");
          client.print(humidity);
          client.print(" %");
          client.print("<br>\r\n");
          client.print("Temperature: ");
          client.print(temperature);
          client.print(" &#8451");//°C
          client.print("<br>\r\n");
          client.print("Heat Index: ");
          client.print(idx_temp);
          client.print(" &#8451");//°C
          client.print("<br>\r\n");
          client.print("</html>\r\n");
          break;
        }
        if (c == '\n') {
          // you're starting a new line
          currentLineIsBlank = true;
        }
        else if (c != '\r') {
          // you've gotten a character on the current line
          currentLineIsBlank = false;
        }
      }
    }
    // give the web browser time to receive the data
    delay(10);

    // close the connection:
    client.stop();
    Serial.println("Client disconnected");
  }
}

void printWifiStatus(){
  // print the SSID of the network you're attached to
  Serial.print("SSID: ");
  Serial.println(WiFi.SSID());

  // print your WiFi shield's IP address
  IPAddress ip = WiFi.localIP();
  Serial.print("IP Address: ");
  Serial.println(ip);
  
  // print where to go in the browser
  Serial.println();
  Serial.print("To see this page in action, open a browser to http://");
  Serial.println(ip);
  Serial.println();
}
