# Fritzing sketch Panneau solaire (saved by Fritzing 0.9.3b)

parts:
  VCC1 = Battery
  Composant1 = Arduino Mega 2560 (Rev3)  # not connected
  Composant2 = Solar Cell
  TP1 = TP4056 [chip_label=TP4056 package="DIP (Dual Inline) [THT]"]

nets:
  N1: VCC1.-, TP1.pin5
  N2: VCC1.+, TP1.pin4
  N3: Composant2.+, TP1.pin1
  N4: Composant2.-, TP1.pin2

custom parts:
  TP4056: A DIP stand-in part for whatever IC you want. With 6 pins on a 300mil dual inline package (DIP) footprint.
